# Fritzing sketch hand (saved by Fritzing 0.9.3b)
breadboards: 3

parts:
  MH-ET_LIVE_ESP32_DEVKIT1 = MH-ET LIVE ESP32 DEVKIT 38 pins
  Pololu_A1 = Pololu A4988 [package=SO16]
  Pololu_A2 = Pololu A4988 [package=SO16]
  Pololu_A3 = Pololu A4988 [package=SO16]
  Pololu_A4 = Pololu A4988 [package=SO16]
  C1 = Capacitor Polarized [package=panasonic_h13]
  SM2 = 28BYJ-48 Stepper Motor [part_number=28BYJ-48]  # not connected
  Driver2 = 28BYJ-48 Driver Module [part_number=ULN2003 package=THT]

nets:
  N1: MH-ET_LIVE_ESP32_DEVKIT1.SVN, Pololu_A4.DIR
  N2: MH-ET_LIVE_ESP32_DEVKIT1.IO34, Pololu_A4.STEP
  N3: MH-ET_LIVE_ESP32_DEVKIT1.IO35, Pololu_A3.DIR
  N4: MH-ET_LIVE_ESP32_DEVKIT1.IO32, Pololu_A3.STEP
  N5: MH-ET_LIVE_ESP32_DEVKIT1.IO33, Pololu_A2.DIR
  N6: MH-ET_LIVE_ESP32_DEVKIT1.IO26, Pololu_A2.STEP
  N7: MH-ET_LIVE_ESP32_DEVKIT1.IO27, Pololu_A1.DIR
  N8: MH-ET_LIVE_ESP32_DEVKIT1.IO14, Pololu_A1.STEP
  N9: MH-ET_LIVE_ESP32_DEVKIT1.IO23, Driver2.IN4
  N10: MH-ET_LIVE_ESP32_DEVKIT1.IO22, Driver2.IN3
  N11: MH-ET_LIVE_ESP32_DEVKIT1.IO21, Driver2.IN2
  N12: MH-ET_LIVE_ESP32_DEVKIT1.IO19, Driver2.IN1
  N13: MH-ET_LIVE_ESP32_DEVKIT1.SD0, Pololu_A1.GND#8, Pololu_A2.GND#8, Pololu_A3.GND#8, Pololu_A4.GND#8
  VDD: MH-ET_LIVE_ESP32_DEVKIT1.SCK, Pololu_A1.MS1, Pololu_A1.VDD, Pololu_A2.MS1, Pololu_A2.VDD, Pololu_A3.MS1, Pololu_A3.VDD, Pololu_A4.MS1, Pololu_A4.VDD
  N14: Pololu_A1.RESET, Pololu_A1.SLEEP
  N15: Pololu_A1.GND#14, Pololu_A2.GND#14, Pololu_A3.GND#14, Pololu_A4.GND#14, C1.-, Driver2.GND
  N16: Pololu_A1.VMOT, Pololu_A2.VMOT, Pololu_A3.VMOT, Pololu_A4.VMOT, C1.+, Driver2.Vmotor
  N17: Pololu_A2.RESET, Pololu_A2.SLEEP
  N18: Pololu_A3.RESET, Pololu_A3.SLEEP
  N19: Pololu_A4.RESET, Pololu_A4.SLEEP

custom parts:
  MH-ET LIVE ESP32 DEVKIT 38 pins: http://mh.nodebb.com/topic/2/mh-et-live-esp32-devkit
  28BYJ-48 Stepper Motor: Unipolar Stepper Motor 28BYJ-48 Top coil - pink & orange Bottom coil - blue & yellow Common rail - red Connector pins: blue - pink - yellow - orange - red
  28BYJ-48 Driver Module: Generic male header
